// Logisim project 2021183642_Fahim Muntashir.circ as structural Verilog
module _7432_OR_gate (
  input  VCC,
  input  in_2,
  input  in_3,
  input  in_4,
  input  in_5,
  input  in_6,
  input  in_7,
  input  in_8,
  input  in_9,
  input  GND,
  output out_11,
  output out_12,
  output out_13,
  output out_14
);

  or or_1 (out_11, in_2, in_3);
  or or_2 (out_12, in_4, in_5);
  or or_3 (out_13, in_6, in_7);
  or or_4 (out_14, in_8, in_9);
endmodule

module _7402_NOR_gate (
  input  Vcc,
  input  in_2,
  input  in_3,
  input  in_4,
  input  in_5,
  input  in_6,
  input  in_7,
  input  in_8,
  input  in_9,
  input  GND,
  output out_11,
  output out_12,
  output out_13,
  output out_14
);

  nor nor_1 (out_11, in_2, in_3);
  nor nor_2 (out_12, in_4, in_5);
  nor nor_3 (out_13, in_6, in_7);
  nor nor_4 (out_14, in_8, in_9);
endmodule

module _7408_AND_gate (
  input  Vcc,
  input  in_2,
  input  in_3,
  input  in_4,
  input  in_5,
  input  in_6,
  input  in_7,
  input  in_8,
  input  in_9,
  input  GND,
  output out_11,
  output out_12,
  output out_13,
  output out_14
);

  and and_1 (out_11, in_2, in_3);
  and and_2 (out_12, in_4, in_5);
  and and_3 (out_13, in_6, in_7);
  and and_4 (out_14, in_8, in_9);
endmodule

module _7400_NAND_gate (
  input  Vcc,
  input  in_2,
  input  in_3,
  input  in_4,
  input  in_5,
  input  in_6,
  input  in_7,
  input  in_8,
  input  in_9,
  input  GND,
  output out_11,
  output out_12,
  output out_13,
  output out_14
);

  nand nand_1 (out_11, in_2, in_3);
  nand nand_2 (out_12, in_4, in_5);
  nand nand_3 (out_13, in_6, in_7);
  nand nand_4 (out_14, in_8, in_9);
endmodule

module _7486_XOR_gate (
  input  Vcc,
  input  in_2,
  input  in_3,
  input  in_4,
  input  in_5,
  input  in_6,
  input  in_7,
  input  in_8,
  input  in_9,
  input  GND,
  output out_11,
  output out_12,
  output out_13,
  output out_14
);

  xor xor_1 (out_11, in_2, in_3);
  xor xor_2 (out_12, in_4, in_5);
  xor xor_3 (out_13, in_6, in_7);
  xor xor_4 (out_14, in_8, in_9);
endmodule

module _7404_NOT_gate (
  input  Vcc,
  input  in_2,
  input  in_3,
  input  in_4,
  input  in_5,
  input  in_6,
  input  in_7,
  input  GND,
  output out_9,
  output out_10,
  output out_11,
  output out_12,
  output out_13,
  output out_14
);

  not not_1 (out_9, in_2);
  not not_2 (out_10, in_3);
  not not_3 (out_11, in_4);
  not not_4 (out_12, in_5);
  not not_5 (out_13, in_6);
  not not_6 (out_14, in_7);
endmodule

module D3 (
  input  A,
  input  B,
  input  C,
  output _6
);

  wire and_1_out, and_2_out, and_3_out, not_1_out, not_2_out, or_1_out;

  not not_1 (not_1_out, A);
  not not_2 (not_2_out, B);
  and and_1 (and_1_out, not_1_out, C);
  and and_2 (and_2_out, A, not_2_out);
  and and_3 (and_3_out, B, C);
  or or_1 (or_1_out, and_1_out, and_2_out);
  or or_2 (_6, or_1_out, and_3_out);

  // Notes on the sheet:
  //   D3: Implimentation of Boolean Functions
  //   1
  //   2
  //   4
  //   3
  //   1
  //   2
  //   4
  //   5
  //   9
  //   10
  //   3
  //   6
  //   8
  //   1
  //   2
  //   3
  //   4
  //   5
endmodule

module D2 (
  input  A,
  input  B,
  input  C,
  input  A_2,
  input  B_2,
  input  C_2,
  output _6,
  output _6_2
);

  wire and_1_out, or_1_out;

  and and_1 (and_1_out, A, B);
  or or_1 (or_1_out, A_2, B_2);
  and and_2 (_6, and_1_out, C);
  or or_2 (_6_2, or_1_out, C_2);

  // Notes on the sheet:
  //   1
  //   2
  //   1
  //   D2: Extension of inputs of AND and OR gates
  //   3
  //   2
  //   4
  //   5
  //   3
  //   4
  //   5
endmodule

module D1 (
  input  A,
  input  B,
  input  A_2,
  input  B_2,
  input  A_3,
  input  A_4,
  input  B_3,
  input  A_5,
  input  B_4,
  input  A_6,
  input  B_5,
  output out_12,
  output out_13,
  output out_14,
  output out_15,
  output out_16,
  output out_17
);

  not not_1 (out_14, A_3);
  and and_1 (out_12, A, B);
  or or_1 (out_13, A_2, B_2);
  nand nand_1 (out_15, A_4, B_3);
  nor nor_1 (out_16, A_5, B_4);
  xor xor_1 (out_17, A_6, B_5);

  // Notes on the sheet:
  //   D1: 
  //   Basic Logic Gates
endmodule

module Lab_Report (
  input  A,
  input  B,
  input  C,
  input  A_2,
  input  B_2,
  input  C_2,
  output ABC__prime,
  output A_B_C__prime
);

  wire nand_1_out, nand_2_out, nor_1_out, nor_2_out;

  nand nand_1 (nand_1_out, A, B);
  nor nor_1 (nor_1_out, A_2, B_2);
  nand nand_2 (nand_2_out, nand_1_out, nand_1_out);
  nor nor_2 (nor_2_out, nor_1_out, nor_1_out);
  nand nand_3 (ABC__prime, nand_2_out, C);
  nor nor_3 (A_B_C__prime, nor_2_out, C_2);

  // Notes on the sheet:
  //   3-input NAND gate with 2-input NAND gate: 
  //   3-input NOR gate with 2-input NOR gate: 
  //   (A.B)'
  //   (A+B)'
  //   A.B
  //   A+B
endmodule
