// Logisim project 2021183642_Fahim Muntashir.circ as structural Verilog: 6 circuits, main circuit main
module main (
  input  A,
  input  B,
  input  C,
  output out_4,
  output p1_Output,
  output p2_Output
);

  wire and_1_out, and_2_out, nand_1_out, nand_2_out, nand_3_out, nand_4_out, nand_5_out, nand_6_out,
       nand_7_out, nand_8_out, nand_10_out, nand_11_out, not_1_out;

  not not_1 (not_1_out, C);
  nand nand_1 (nand_1_out, A, C);
  nand nand_2 (nand_2_out, C, C);
  nand nand_3 (nand_3_out, C, C);
  nand nand_4 (nand_4_out, B, nand_2_out);
  nand nand_5 (nand_5_out, A, C);
  nand nand_6 (nand_6_out, B, nand_3_out);
  and and_1 (and_1_out, A, C);
  and and_2 (and_2_out, B, not_1_out);
  nand nand_7 (nand_7_out, nand_1_out, nand_1_out);
  nand nand_8 (nand_8_out, nand_4_out, nand_4_out);
  or or_1 (out_4, and_1_out, and_2_out);
  nand nand_9 (p2_Output, nand_5_out, nand_6_out);
  nand nand_10 (nand_10_out, nand_7_out, nand_7_out);
  nand nand_11 (nand_11_out, nand_8_out, nand_8_out);
  nand nand_12 (p1_Output, nand_10_out, nand_11_out);
endmodule

module experiment (
  input  A,
  input  A_2,
  input  A_3,
  input  B,
  input  B_2,
  input  A_4,
  input  A_5,
  input  B_3,
  input  B_4,
  output A_prime,
  output A_B,
  output AB,
  output F,
  output F_2
);

  wire nand_1_out, nand_2_out, nand_3_out, nand_5_out, nand_6_out, nand_7_out, nand_8_out, nor_2_out,
       nor_3_out, nor_5_out;

  nor nor_1 (A_prime, A, A);
  nand nand_1 (nand_1_out, A_4, B_3);
  nand nand_2 (nand_2_out, A_4, nand_1_out);
  nand nand_3 (nand_3_out, nand_1_out, B_3);
  nor nor_2 (nor_2_out, A_2, A_2);
  nor nor_3 (nor_3_out, B_2, B_2);
  nand nand_4 (F, nand_2_out, nand_3_out);
  nor nor_4 (AB, nor_2_out, nor_3_out);
  nand nand_5 (nand_5_out, A_5, B_4);
  nor nor_5 (nor_5_out, A_3, B);
  nand nand_6 (nand_6_out, A_5, nand_5_out);
  nand nand_7 (nand_7_out, nand_5_out, B_4);
  nor nor_6 (A_B, nor_5_out, nor_5_out);
  nand nand_8 (nand_8_out, nand_6_out, nand_7_out);
  nand nand_9 (F_2, nand_8_out, nand_8_out);

  // Notes on the sheet:
  //   NOT
  //   (AB)'
  //   XOR
  //   (A.AB')'
  //   (B.AB')'
  //   A'
  //   B'
  //   AND
  //   (AB'+A'B)
  //   (A'+B')'
  //   (AB)'
  //   XNOR
  //   (A+B)'
  //   OR
  //   (A.(AB)')'
  //   ((AB)'B')'
  //   A xnor B
endmodule

module _1s (
  input  A,
  input  B,
  input  A_2,
  input  B_2,
  output F,
  output F_2
);

  wire nand_1_out, nand_2_out, nand_3_out, nand_4_out, nand_5_out, nand_6_out, nand_8_out;

  nand nand_1 (nand_1_out, A_2, B_2);
  nand nand_2 (nand_2_out, A, B);
  nand nand_3 (nand_3_out, A_2, nand_1_out);
  nand nand_4 (nand_4_out, nand_1_out, B_2);
  nand nand_5 (nand_5_out, A, nand_2_out);
  nand nand_6 (nand_6_out, nand_2_out, B);
  nand nand_7 (F, nand_5_out, nand_6_out);
  nand nand_8 (nand_8_out, nand_3_out, nand_4_out);
  nand nand_9 (F_2, nand_8_out, nand_8_out);

  // Notes on the sheet:
  //   XOR
  //   XNOR
endmodule

module \nor  (
  input  A,
  input  B,
  input  in_3,
  input  in_4,
  output F,
  output F_2
);

  wire nor_1_out, nor_2_out, nor_3_out, nor_4_out, nor_5_out, nor_6_out, nor_7_out, nor_8_out, nor_9_out;

  nor nor_1 (nor_1_out, in_3, in_3);
  nor nor_2 (nor_2_out, in_4, in_4);
  nor nor_3 (nor_3_out, in_3, in_4);
  nor nor_4 (nor_4_out, A, B);
  nor nor_5 (nor_5_out, nor_1_out, nor_2_out);
  nor nor_6 (nor_6_out, nor_4_out, A);
  nor nor_7 (nor_7_out, nor_4_out, B);
  nor nor_8 (nor_8_out, nor_5_out, nor_3_out);
  nor nor_9 (nor_9_out, nor_6_out, nor_7_out);
  nor nor_10 (F_2, nor_8_out, nor_8_out);
  nor nor_11 (F, nor_9_out, nor_9_out);

  // Notes on the sheet:
  //   XNOR 
  //   XOR
endmodule

module q (
  input  A,
  input  B,
  input  C,
  output p1_Output
);

  wire nand_1_out, nand_2_out, nand_3_out, nand_4_out, nand_5_out, nand_6_out, nand_7_out;

  nand nand_1 (nand_1_out, A, C);
  nand nand_2 (nand_2_out, C, C);
  nand nand_3 (nand_3_out, B, nand_2_out);
  nand nand_4 (nand_4_out, nand_1_out, nand_1_out);
  nand nand_5 (nand_5_out, nand_3_out, nand_3_out);
  nand nand_6 (nand_6_out, nand_4_out, nand_4_out);
  nand nand_7 (nand_7_out, nand_5_out, nand_5_out);
  nand nand_8 (p1_Output, nand_6_out, nand_7_out);

  // Notes on the sheet:
  //   (AC)'
  //   (BC')'
  //   AC
  //   Part 1
  //   B'C
  //   (AC)'
  //   BC'
  //   BC'+AC
endmodule

module q3 (
  input  A,
  input  B,
  input  C,
  output p2_Output
);

  wire nand_1_out, nand_2_out, nand_3_out;

  nand nand_1 (nand_1_out, C, C);
  nand nand_2 (nand_2_out, A, C);
  nand nand_3 (nand_3_out, B, nand_1_out);
  nand nand_4 (p2_Output, nand_2_out, nand_3_out);

  // Notes on the sheet:
  //   Part 2
  //   (AC)'
  //   (BC')'
  //   BC'+AC
endmodule
