// Logisim project 2021183642_Fahim Muntashir.circ as structural Verilog: 3 circuits, main circuit main
module main (
  input  A,
  input  B,
  input  C,
  output Min_Term,
  output Max_Term
);

  wire and_1_out, and_2_out, and_3_out, and_4_out, not_1_out, not_2_out, not_3_out, or_1_out, or_2_out,
       or_3_out, or_4_out, or_5_out;

  not not_1 (not_1_out, A);
  not not_2 (not_2_out, B);
  not not_3 (not_3_out, C);
  and and_1 (and_1_out, not_1_out, not_2_out, C);
  and and_2 (and_2_out, not_1_out, B, not_3_out);
  and and_3 (and_3_out, A, B, not_3_out);
  or or_1 (or_1_out, A, B, C);
  or or_2 (or_2_out, A, not_2_out, not_3_out);
  or or_3 (or_3_out, not_1_out, B, C);
  or or_4 (or_4_out, not_1_out, B, not_3_out);
  or or_5 (or_5_out, not_1_out, not_2_out, not_3_out);
  or or_6 (Min_Term, and_1_out, and_2_out, and_3_out);
  and and_4 (and_4_out, or_1_out, or_2_out, or_3_out);
  and and_5 (Max_Term, and_4_out, or_4_out, or_5_out);
endmodule

module _1st (
  input  A,
  input  B,
  input  C,
  output Min_Term
);

  wire and_1_out, and_2_out, and_3_out, not_1_out, not_2_out, not_3_out;

  not not_1 (not_1_out, A);
  not not_2 (not_2_out, B);
  not not_3 (not_3_out, C);
  and and_1 (and_1_out, not_1_out, not_2_out, C);
  and and_2 (and_2_out, not_1_out, B, not_3_out);
  and and_3 (and_3_out, A, B, not_3_out);
  or or_1 (Min_Term, and_1_out, and_2_out, and_3_out);

  // Notes on the sheet:
  //   A'B'C
  //   A'BC'
  //   1st Canonical Form
  //   ABC'
  //   A'B'C+A'BC'+ABC'
endmodule

module _2nd (
  input  A,
  input  B,
  input  C,
  output Max_Term
);

  wire and_1_out, not_1_out, not_2_out, not_3_out, or_1_out, or_2_out, or_3_out, or_4_out, or_5_out;

  not not_1 (not_1_out, A);
  not not_2 (not_2_out, B);
  not not_3 (not_3_out, C);
  or or_1 (or_1_out, A, B, C);
  or or_2 (or_2_out, A, not_2_out, not_3_out);
  or or_3 (or_3_out, not_1_out, B, C);
  or or_4 (or_4_out, not_1_out, B, not_3_out);
  or or_5 (or_5_out, not_1_out, not_2_out, not_3_out);
  and and_1 (and_1_out, or_1_out, or_2_out, or_3_out);
  and and_2 (Max_Term, and_1_out, or_4_out, or_5_out);

  // Notes on the sheet:
  //   A+B+C
  //   A+B'+C'
  //   A'+B+C
  //   A'+B+C'
  //   A'+B'+C'
  //   2nd Canonical Form
  //   (A+B+C).(A+B'+C').(A'+B+C).(A'+B+C').(A'+B'+C')
endmodule
