// Logisim project 2021183642_Fahim Muntashir.circ as structural Verilog
module main (
  input  W,
  input  X,
  input  Y,
  input  Z,
  output A,
  output B,
  output C,
  output D
);

  wire and_1_out, and_2_out, and_3_out, and_4_out, and_5_out, and_6_out, and_7_out, not_1_out, not_2_out,
       not_3_out, not_4_out, not_5_out, not_6_out;

  not not_1 (not_1_out, X);
  not not_2 (not_2_out, X);
  not not_3 (not_3_out, Y);
  not not_4 (not_4_out, Z);
  and and_1 (and_1_out, X, Z);
  and and_2 (and_2_out, X, Y);
  and and_3 (and_3_out, not_1_out, Z);
  and and_4 (and_4_out, not_2_out, Y);
  and and_5 (and_5_out, X, not_3_out, not_4_out);
  not not_5 (not_5_out, Y);
  not not_6 (not_6_out, Z);
  and and_6 (and_6_out, not_5_out, not_6_out);
  and and_7 (and_7_out, Y, Z);
  not not_7 (D, Z);
  or or_1 (A, W, and_1_out, and_2_out);
  or or_2 (B, and_3_out, and_4_out, and_5_out);
  or or_3 (C, and_6_out, and_7_out);

  // Notes on the sheet:
  //   Figure F2: Minimal 1st canonical circuit of BCD to EXCESS-3 converter
  //   XZ
  //   XY
  //   X'Z
  //   W
  //   X'Y
  //   XY'Z'
  //   Y'Z'
  //   YZ
  //   W+XZ+XY
  //   Z'
  //   X'Z+X'Y+XY'Z'
  //   Y'Z'+YZ
endmodule
