// Logisim project 2021183642_Fahim Muntashir.circ as structural Verilog: 2 circuits, main circuit main
module main (
  input  A1,
  input  A2,
  input  A3,
  input  A4,
  input  B1,
  input  B2,
  input  B3,
  input  B4,
  input  C0,
  output S4,
  output S3,
  output S2,
  output S1,
  output C4
);

  wire xor_1_out, xor_2_out, xor_3_out, xor_4_out;

  xor xor_1 (xor_1_out, B1, C0);
  xor xor_2 (xor_2_out, B2, C0);
  xor xor_3 (xor_3_out, B3, C0);
  xor xor_4 (xor_4_out, B4, C0);
  Adder #(.width(1)) adder_1 (.a(A1), .b(xor_1_out), .out(S1), .cin(C0));  // open: cout
  Adder #(.width(1)) adder_2 (.a(A2), .b(xor_2_out), .out(S2));  // open: cin, cout
  Adder #(.width(1)) adder_3 (.a(A3), .b(xor_3_out), .out(S3));  // open: cin, cout
  Adder #(.width(1)) adder_4 (.a(A4), .b(xor_4_out), .out(S4), .cout(C4));  // open: cin

  // Notes on the sheet:
  //   4-bit Adder Subtractor
endmodule

module e2 (
  input  A4,
  input  A3,
  input  A2,
  input  A1,
  input  B4,
  input  B3,
  input  B2,
  input  B1,
  output C,
  output S4,
  output S3,
  output S2,
  output S1
);

  wire adder_1_cout, adder_1_out, adder_2_cout, adder_2_out, adder_3_cout, adder_3_out, adder_4_cout,
       adder_4_out, adder_5_cout, adder_6_cout, adder_7_cout, and_1_out, and_2_out;

  Adder #(.width(1)) adder_1 (.a(A1), .b(B1), .out(adder_1_out), .cin(1'b0), .cout(adder_1_cout));
  Adder #(.width(1)) adder_2 (.a(A2), .b(B2), .out(adder_2_out), .cin(adder_1_cout), .cout(adder_2_cout));
  Adder #(.width(1)) adder_3 (.a(A3), .b(B3), .out(adder_3_out), .cin(adder_2_cout), .cout(adder_3_cout));
  Adder #(.width(1)) adder_4 (.a(A4), .b(B4), .out(adder_4_out), .cin(adder_3_cout), .cout(adder_4_cout));
  and and_1 (and_1_out, adder_2_out, adder_4_out);
  and and_2 (and_2_out, adder_3_out, adder_4_out);
  or or_1 (C, adder_4_cout, and_1_out, and_2_out);
  Adder #(.width(1)) adder_5 (.a(adder_1_out), .b(1'b0), .out(S1), .cin(1'b0), .cout(adder_5_cout));
  Adder #(.width(1)) adder_6 (.a(adder_2_out), .b(C), .out(S2), .cin(adder_5_cout), .cout(adder_6_cout));
  Adder #(.width(1)) adder_7 (.a(adder_3_out), .b(C), .out(S3), .cin(adder_6_cout), .cout(adder_7_cout));
  Adder #(.width(1)) adder_8 (.a(adder_4_out), .b(1'b0), .out(S4), .cin(adder_7_cout));  // open: cout

  // Notes on the sheet:
  //   BCD Adder
endmodule
