// Logisim project 2021183642_Fahim Muntashir.circ as structural Verilog: 4 circuits, main circuit main
module main (
  input  in_1,
  input  in_2,
  input  K,
  input  [3:0] in_4,
  output out_5
);

  wire clock_1_out;

  Clock clock_1 (.out(clock_1_out));
  D_Flip_Flop d_ff_1 (.clk(clock_1_out), .D(in_1), .Q(in_4[3]), .preset(in_2), .reset(K));  // open: Qn, en
  D_Flip_Flop d_ff_2 (.clk(clock_1_out), .D(in_4[3]), .Q(in_4[2]), .preset(in_2), .reset(K));  // open: Qn, en
  D_Flip_Flop d_ff_3 (.clk(clock_1_out), .D(in_4[2]), .Q(in_4[1]), .preset(in_2), .reset(K));  // open: Qn, en
  D_Flip_Flop d_ff_4 (.clk(clock_1_out), .D(in_4[1]), .Q(in_4[0]), .preset(in_2), .reset(K));  // open: Qn, en

  assign out_5 = in_4[0];
endmodule

module exp_1 (
  input  K,
  input  J,
  input  K_2,
  input  J_2,
  output Q,
  output Q_2,
  output Q_3,
  output Q_prime
);

  wire and_1_out, and_2_out, clock_1_out, clock_2_out;

  Clock clock_1 (.out(clock_1_out));
  and and_1 (and_1_out, Q, K, clock_1_out);
  and and_2 (and_2_out, clock_1_out, J_2, Q_prime);
  nor nor_1 (Q, and_1_out, Q_prime);
  nor nor_2 (Q_prime, Q, and_2_out);
  Clock clock_2 (.out(clock_2_out));
  J_K_Flip_Flop j_k_ff_1 (.J(J), .clk(clock_2_out), .K(K_2), .Q(Q_2), .Qn(Q_3));  // open: preset, en, reset

  // Notes on the sheet:
  //   Experiment 1
endmodule

module exp_2 (
  input  T,
  input  T_2,
  input  T_3,
  input  D,
  input  D_2,
  input  D_3,
  output Q,
  output Q_prime,
  output Q_2,
  output Q_prime_2,
  output Q_3,
  output Q_prime_3,
  output Q_4,
  output Q_5,
  output Q_prime_4,
  output Q_prime_5,
  output Q_6,
  output Q_prime_6
);

  wire and_1_out, and_2_out, and_3_out, and_4_out, clock_1_out, clock_2_out, clock_3_out, clock_4_out,
       clock_5_out, clock_6_out, not_1_out, not_2_out;

  not not_1 (not_1_out, D_2);
  Clock clock_1 (.out(clock_1_out));
  Clock clock_2 (.out(clock_2_out));
  and and_1 (and_1_out, Q_4, not_1_out, clock_2_out);
  and and_2 (and_2_out, clock_2_out, D_2, Q_prime_5);
  and and_3 (and_3_out, Q_2, T_2, clock_1_out);
  and and_4 (and_4_out, clock_1_out, T_2, Q_prime_2);
  nor nor_1 (Q_2, and_3_out, Q_prime_2);
  nor nor_2 (Q_prime_2, Q_2, and_4_out);
  nor nor_3 (Q_4, and_1_out, Q_prime_5);
  nor nor_4 (Q_prime_5, Q_4, and_2_out);
  not not_2 (not_2_out, D_3);
  Clock clock_3 (.out(clock_3_out));
  Clock clock_4 (.out(clock_4_out));
  Clock clock_5 (.out(clock_5_out));
  Clock clock_6 (.out(clock_6_out));
  T_Flip_Flop t_ff_1 (.clk(clock_3_out), .T(T), .Q(Q), .Qn(Q_prime));  // open: preset, reset, en
  J_K_Flip_Flop j_k_ff_1 (.J(T_3), .clk(clock_4_out), .K(T_3), .Q(Q_3), .Qn(Q_prime_3));  // open: preset, en, reset
  D_Flip_Flop d_ff_1 (.clk(clock_5_out), .D(D), .Q(Q_5), .Qn(Q_prime_4));  // open: preset, en, reset
  J_K_Flip_Flop j_k_ff_2 (
    .J(D_3), .clk(clock_6_out), .K(not_2_out), .Q(Q_6), .Qn(Q_prime_6));  // open: preset, en, reset

  // Notes on the sheet:
  //   T Flip-Flop
  //   D Flip-Flip
  //   Experiment 3
  //   T Flip-Flop using T Flip-Flop
  //   D Flip-Flop using D Flip-Flop
  //   D Flip-Flop using JK Flip-Flop
  //   T Flip-Flop using JK Flip-Flop
endmodule

module exp_3 (
  input  S_input,
  input  in_2,
  output S_Output,
  output Q
);

  wire clock_1_out, clock_2_out, d_ff_1_q, d_ff_3_q, d_ff_4_q, d_ff_5_q, d_ff_6_q, d_ff_7_q;

  Clock clock_1 (.out(clock_1_out));
  D_Flip_Flop d_ff_1 (.clk(clock_1_out), .D(in_2), .Q(d_ff_1_q));  // open: Qn, preset, en, reset
  D_Flip_Flop d_ff_2 (.clk(clock_2_out), .D(d_ff_4_q), .Q(S_Output));  // open: Qn, preset, en, reset
  D_Flip_Flop d_ff_3 (.clk(clock_1_out), .D(d_ff_1_q), .Q(d_ff_3_q));  // open: Qn, preset, en, reset
  D_Flip_Flop d_ff_4 (.clk(clock_2_out), .D(d_ff_5_q), .Q(d_ff_4_q));  // open: Qn, preset, en, reset
  D_Flip_Flop d_ff_5 (.clk(clock_2_out), .D(d_ff_7_q), .Q(d_ff_5_q));  // open: Qn, preset, en, reset
  D_Flip_Flop d_ff_6 (.clk(clock_1_out), .D(d_ff_3_q), .Q(d_ff_6_q));  // open: Qn, preset, en, reset
  Clock clock_2 (.out(clock_2_out));
  D_Flip_Flop d_ff_7 (.clk(clock_2_out), .D(S_input), .Q(d_ff_7_q));  // open: Qn, preset, en, reset
  D_Flip_Flop d_ff_8 (.clk(clock_1_out), .D(d_ff_6_q), .Q(Q));  // open: Qn, preset, en, reset

  // Notes on the sheet:
  //   Experiment 3
endmodule
