// Logisim project 2021183642_Fahim Muntashir.circ as structural Verilog
module exp_1 (
  input  X,
  output A,
  output Y,
  output B
);

  wire and_1_out, clock_1_out, j_k_ff_1_qn, not_1_out;

  not not_1 (not_1_out, X);
  Clock clock_1 (.out(clock_1_out));
  and and_1 (and_1_out, j_k_ff_1_qn, not_1_out);
  J_K_Flip_Flop j_k_ff_1 (.J(X), .clk(clock_1_out), .K(X), .Q(A), .Qn(j_k_ff_1_qn));  // open: preset, en, reset
  J_K_Flip_Flop j_k_ff_2 (.J(and_1_out), .clk(clock_1_out), .K(X), .Q(B));  // open: Qn, preset, en, reset
  and and_2 (Y, j_k_ff_1_qn, X);
endmodule

module exp_2 (
  input  X,
  output A,
  output Y,
  output B
);

  wire and_1_out, and_2_out, clock_1_out, j_k_ff_1_qn, j_k_ff_2_qn, not_1_out, or_1_out;

  not not_1 (not_1_out, X);
  and and_1 (and_1_out, j_k_ff_1_qn, not_1_out, j_k_ff_2_qn);
  and and_2 (and_2_out, X, B);
  Clock clock_1 (.out(clock_1_out));
  or or_1 (or_1_out, and_1_out, and_2_out);
  J_K_Flip_Flop j_k_ff_1 (.J(X), .clk(clock_1_out), .Q(A), .Qn(j_k_ff_1_qn));  // open: K, preset, en, reset
  J_K_Flip_Flop j_k_ff_2 (.J(or_1_out), .K(clock_1_out), .Q(B), .Qn(j_k_ff_2_qn));  // open: clk, preset, en, reset
  and and_3 (Y, j_k_ff_1_qn, not_1_out);
endmodule
