// Logisim project Phase 1.circ as structural Verilog: 11 circuits, main circuit main
module main (
  input  A,
  input  B,
  input  C
);

  wire multiplexer_1_out, multiplexer_2_out, multiplexer_3_out, multiplexer_4_out, multiplexer_5_out,
       multiplexer_6_out, multiplexer_7_out, not_1_out, not_2_out, not_3_out;

  not not_1 (not_1_out, A);
  not not_2 (not_2_out, C);
  not not_3 (not_3_out, B);
  Multiplexer #(.select(2), .enable("false")) multiplexer_1 (
    .in0(C), .in1(1'b0), .in2(C), .in3(not_2_out), .out(multiplexer_1_out), .sel({A, B}));
  Multiplexer #(.select(2), .enable("false")) multiplexer_2 (
    .in0(A), .in1(A), .in2(A), .in3(A), .out(multiplexer_2_out), .sel({B, C}));
  Multiplexer #(.select(2), .enable("false")) multiplexer_3 (
    .in0(B), .in1(B), .in2(not_3_out), .in3(B), .out(multiplexer_3_out), .sel({A, C}));
  Multiplexer #(.select(2), .enable("false")) multiplexer_4 (
    .in0(1'b0), .in1(1'b0), .in2(C), .in3(not_2_out), .out(multiplexer_4_out), .sel({A, B}));
  Multiplexer #(.select(2), .enable("false")) multiplexer_5 (
    .in0(C), .in1(1'b1), .in2(1'b0), .in3(not_2_out), .out(multiplexer_5_out), .sel({A, B}));
  Multiplexer #(.select(2), .enable("false")) multiplexer_6 (
    .in0(C), .in1(C), .in2(not_2_out), .in3(not_2_out), .out(multiplexer_6_out), .sel({A, B}));
  Multiplexer #(.select(2), .enable("false")) multiplexer_7 (
    .in0(C), .in1(1'b1), .in2(1'b1), .in3(not_2_out), .out(multiplexer_7_out), .sel({A, B}));
  _7_Segment_Display u_7_segment_display_1 (
    .g(multiplexer_7_out), .f(multiplexer_6_out), .a(multiplexer_1_out), .b(multiplexer_2_out),
    .e(multiplexer_5_out), .d(multiplexer_4_out), .c(multiplexer_3_out));  // open: dp
endmodule

module Generalized_SOP (
  input  A,
  input  B,
  input  C
);

  wire and_1_out, and_2_out, and_3_out, and_4_out, and_5_out, and_6_out, and_7_out, and_8_out, and_9_out,
       and_10_out, and_11_out, and_12_out, and_13_out, and_14_out, and_15_out, and_16_out, and_17_out,
       and_18_out, and_19_out, and_20_out, and_21_out, and_22_out, and_23_out, and_24_out, and_25_out,
       and_26_out, and_27_out, and_28_out, and_29_out, not_1_out, not_2_out, not_3_out, or_1_out, or_2_out,
       or_3_out, or_4_out, or_5_out, or_6_out, or_7_out, or_8_out, or_9_out, or_10_out, or_11_out, or_12_out,
       or_13_out, or_14_out;

  not not_1 (not_1_out, A);
  not not_2 (not_2_out, B);
  not not_3 (not_3_out, C);
  and and_1 (and_1_out, not_1_out, not_2_out, C);
  and and_2 (and_2_out, A, not_2_out, C);
  and and_3 (and_3_out, A, B, not_3_out);
  and and_4 (and_4_out, A, not_2_out, not_3_out);
  and and_5 (and_5_out, A, not_2_out, C);
  and and_6 (and_6_out, A, B, not_3_out);
  and and_7 (and_7_out, A, B, C);
  and and_8 (and_8_out, not_1_out, B, not_3_out);
  and and_9 (and_9_out, not_1_out, B, C);
  and and_10 (and_10_out, A, not_2_out, not_3_out);
  and and_11 (and_11_out, A, not_2_out, C);
  and and_12 (and_12_out, A, B, not_3_out);
  and and_13 (and_13_out, A, B, C);
  and and_14 (and_14_out, A, not_2_out, C);
  and and_15 (and_15_out, A, B, not_3_out);
  and and_16 (and_16_out, not_1_out, not_2_out, C);
  and and_17 (and_17_out, not_1_out, B, not_3_out);
  and and_18 (and_18_out, not_1_out, B, C);
  and and_19 (and_19_out, A, B, not_3_out);
  and and_20 (and_20_out, not_1_out, not_2_out, C);
  and and_21 (and_21_out, not_1_out, B, C);
  and and_22 (and_22_out, A, not_2_out, not_3_out);
  and and_23 (and_23_out, A, B, not_3_out);
  and and_24 (and_24_out, not_1_out, not_2_out, C);
  and and_25 (and_25_out, not_1_out, B, not_3_out);
  and and_26 (and_26_out, not_1_out, B, C);
  and and_27 (and_27_out, A, not_2_out, not_3_out);
  and and_28 (and_28_out, A, not_2_out, C);
  and and_29 (and_29_out, A, B, not_3_out);
  or or_1 (or_1_out, and_1_out, and_2_out, and_3_out);
  or or_2 (or_2_out, and_14_out, and_15_out);
  or or_3 (or_3_out, and_16_out, and_17_out, and_18_out);
  or or_4 (or_4_out, and_20_out, and_21_out, and_22_out);
  or or_5 (or_5_out, and_4_out, and_5_out, and_6_out);
  or or_6 (or_6_out, and_8_out, and_9_out, and_10_out);
  or or_7 (or_7_out, and_11_out, and_12_out, and_13_out);
  or or_8 (or_8_out, or_3_out, and_19_out);
  or or_9 (or_9_out, or_4_out, and_23_out);
  or or_10 (or_10_out, and_24_out, and_25_out, and_26_out);
  or or_11 (or_11_out, and_27_out, and_28_out, and_29_out);
  or or_12 (or_12_out, or_5_out, and_7_out);
  or or_13 (or_13_out, or_6_out, or_7_out);
  or or_14 (or_14_out, or_10_out, or_11_out);
  _7_Segment_Display u_7_segment_display_1 (
    .g(or_14_out), .f(or_9_out), .a(or_1_out), .b(or_12_out), .e(or_8_out), .d(or_2_out), .c(or_13_out));  // open: dp

  // Notes on the sheet:
  //   a
  //   d
  //   b
  //   e
  //   f
  //   c
  //   g
endmodule

module Simplified_SOP (
  input  A,
  input  B,
  input  C
);

  wire and_1_out, and_2_out, and_3_out, and_4_out, and_5_out, and_6_out, and_7_out, and_8_out, and_9_out,
       and_10_out, and_11_out, not_1_out, not_2_out, not_3_out, or_1_out, or_2_out, or_3_out, or_4_out,
       or_5_out, or_6_out;

  not not_1 (not_1_out, A);
  not not_2 (not_2_out, B);
  not not_3 (not_3_out, C);
  and and_1 (and_1_out, A, B, not_3_out);
  and and_2 (and_2_out, not_2_out, C);
  and and_3 (and_3_out, A, not_2_out, C);
  and and_4 (and_4_out, A, B, not_3_out);
  and and_5 (and_5_out, not_1_out, C);
  and and_6 (and_6_out, B, not_3_out);
  and and_7 (and_7_out, not_1_out, C);
  and and_8 (and_8_out, A, not_3_out);
  and and_9 (and_9_out, not_1_out, C);
  and and_10 (and_10_out, B, not_3_out);
  and and_11 (and_11_out, A, not_2_out);
  or or_1 (or_1_out, and_1_out, and_2_out);
  or or_2 (or_2_out, A, B);
  or or_3 (or_3_out, and_3_out, and_4_out);
  or or_4 (or_4_out, and_5_out, and_6_out);
  or or_5 (or_5_out, and_7_out, and_8_out);
  or or_6 (or_6_out, and_9_out, and_10_out, and_11_out);
  _7_Segment_Display u_7_segment_display_1 (
    .g(or_6_out), .f(or_5_out), .a(or_1_out), .b(A), .e(or_4_out), .d(or_3_out), .c(or_2_out));  // open: dp

  // Notes on the sheet:
  //   a
  //   b
  //   c
  //   d
  //   e
  //   f
  //   g
endmodule

module Generalized_POS (
  input  A,
  input  B,
  input  C
);

  wire and_1_out, and_2_out, and_3_out, and_4_out, and_5_out, and_6_out, and_7_out, and_8_out, and_9_out,
       and_10_out, and_11_out, and_12_out, and_13_out, not_1_out, not_2_out, not_3_out, or_1_out, or_2_out,
       or_3_out, or_4_out, or_5_out, or_6_out, or_7_out, or_8_out, or_9_out, or_10_out, or_11_out, or_12_out,
       or_13_out, or_14_out, or_15_out, or_16_out, or_17_out, or_18_out, or_19_out, or_20_out, or_21_out,
       or_22_out, or_23_out, or_24_out, or_25_out, or_26_out, or_27_out;

  not not_1 (not_1_out, A);
  not not_2 (not_2_out, B);
  not not_3 (not_3_out, C);
  or or_1 (or_1_out, not_1_out, not_2_out, not_3_out);
  or or_2 (or_2_out, A, not_2_out, C);
  or or_3 (or_3_out, A, not_2_out, not_3_out);
  or or_4 (or_4_out, not_1_out, B, C);
  or or_5 (or_5_out, A, B, C);
  or or_6 (or_6_out, A, not_2_out, not_3_out);
  or or_7 (or_7_out, A, not_2_out, C);
  or or_8 (or_8_out, A, B, not_3_out);
  or or_9 (or_9_out, A, B, C);
  or or_10 (or_10_out, A, B, C);
  or or_11 (or_11_out, A, B, not_3_out);
  or or_12 (or_12_out, not_1_out, not_2_out, not_3_out);
  or or_13 (or_13_out, A, B, not_3_out);
  or or_14 (or_14_out, A, not_2_out, C);
  or or_15 (or_15_out, A, not_2_out, not_3_out);
  or or_16 (or_16_out, not_1_out, B, C);
  or or_17 (or_17_out, A, B, C);
  or or_18 (or_18_out, not_1_out, not_2_out, not_3_out);
  or or_19 (or_19_out, not_1_out, B, not_3_out);
  or or_20 (or_20_out, not_1_out, B, C);
  or or_21 (or_21_out, A, B, C);
  or or_22 (or_22_out, not_1_out, not_2_out, not_3_out);
  or or_23 (or_23_out, A, not_2_out, C);
  or or_24 (or_24_out, not_1_out, B, not_3_out);
  or or_25 (or_25_out, A, B, C);
  or or_26 (or_26_out, not_1_out, not_2_out, not_3_out);
  or or_27 (or_27_out, A, B, C);
  and and_1 (and_1_out, or_1_out, or_2_out, or_3_out);
  and and_2 (and_2_out, or_6_out, or_7_out, or_8_out);
  and and_3 (and_3_out, or_10_out, or_11_out);
  and and_4 (and_4_out, or_12_out, or_13_out, or_14_out);
  and and_5 (and_5_out, or_15_out, or_16_out, or_17_out);
  and and_6 (and_6_out, or_18_out, or_19_out, or_20_out);
  and and_7 (and_7_out, or_22_out, or_23_out, or_24_out);
  and and_8 (and_8_out, or_26_out, or_27_out);
  and and_9 (and_9_out, and_1_out, or_4_out, or_5_out);
  and and_10 (and_10_out, and_2_out, or_9_out);
  and and_11 (and_11_out, and_6_out, or_21_out);
  and and_12 (and_12_out, and_7_out, or_25_out);
  and and_13 (and_13_out, and_4_out, and_5_out);
  _7_Segment_Display u_7_segment_display_1 (
    .g(and_8_out), .f(and_12_out), .a(and_9_out), .b(and_10_out), .e(and_11_out), .d(and_13_out),
    .c(and_3_out));  // open: dp

  // Notes on the sheet:
  //   g
  //   c
  //   f
  //   a
  //   b
  //   d
  //   e
endmodule

module Simplified_POS (
  input  A,
  input  B,
  input  C
);

  wire and_1_out, and_2_out, and_3_out, and_4_out, and_5_out, not_1_out, not_2_out, not_3_out, or_1_out,
       or_2_out, or_3_out, or_4_out, or_5_out, or_6_out, or_7_out, or_8_out, or_9_out, or_10_out, or_11_out,
       or_12_out;

  not not_1 (not_1_out, A);
  not not_2 (not_2_out, B);
  not not_3 (not_3_out, C);
  or or_1 (or_1_out, A, C);
  or or_2 (or_2_out, B, C);
  or or_3 (or_3_out, not_2_out, not_3_out);
  or or_4 (or_4_out, A, B);
  or or_5 (or_5_out, B, C);
  or or_6 (or_6_out, not_2_out, not_3_out);
  or or_7 (or_7_out, B, C);
  or or_8 (or_8_out, not_1_out, not_3_out);
  or or_9 (or_9_out, A, C);
  or or_10 (or_10_out, not_1_out, not_3_out);
  or or_11 (or_11_out, A, B, C);
  or or_12 (or_12_out, not_1_out, not_2_out, not_3_out);
  and and_1 (and_1_out, or_1_out, or_2_out, or_3_out);
  and and_2 (and_2_out, A, or_5_out, or_6_out);
  and and_3 (and_3_out, or_7_out, or_8_out);
  and and_4 (and_4_out, or_9_out, or_10_out);
  and and_5 (and_5_out, or_11_out, or_12_out);
  _7_Segment_Display u_7_segment_display_1 (
    .g(and_5_out), .f(and_4_out), .a(and_1_out), .b(A), .e(and_3_out), .d(and_2_out), .c(or_4_out));  // open: dp

  // Notes on the sheet:
  //   b
  //   c
  //   e
  //   f
  //   a
  //   d
  //   g
endmodule

module Simplified_SOP_using_NAND_gate (
  input  A,
  input  B,
  input  C,
  input  A_2,
  input  B_2,
  input  C_2
);

  wire nand_1_out, nand_2_out, nand_3_out, nand_4_out, nand_5_out, nand_6_out, nand_7_out, nand_8_out,
       nand_9_out, nand_10_out, nand_11_out, nand_12_out, nand_13_out, nand_14_out, nand_15_out, nand_16_out,
       nand_17_out, nand_18_out, nand_19_out, nand_20_out, nand_21_out, nand_22_out, nand_23_out,
       nand_24_out, nand_25_out, nand_26_out, nand_27_out, nand_28_out, nand_29_out, nand_30_out,
       nand_31_out, nand_32_out, nand_33_out, nand_34_out, nand_35_out, nand_36_out, nand_37_out,
       nand_38_out, nand_39_out, nand_40_out, nand_41_out, nand_42_out, nand_43_out, nand_44_out,
       nand_45_out, nand_46_out, nand_47_out, nand_48_out, nand_49_out, nand_50_out, nand_51_out,
       nand_52_out, nand_53_out, nand_54_out, nand_55_out, nand_56_out, nand_57_out, nand_58_out,
       nand_59_out, nand_60_out, nand_61_out, nand_62_out, nand_63_out, nand_64_out, nand_65_out, nand_66_out;

  nand nand_1 (nand_1_out, A_2, A_2);
  nand nand_2 (nand_2_out, B_2, B_2);
  nand nand_3 (nand_3_out, C_2, C_2);
  nand nand_4 (nand_4_out, A_2, B_2, nand_3_out);
  nand nand_5 (nand_5_out, nand_2_out, C_2);
  nand nand_6 (nand_6_out, A_2, A_2);
  nand nand_7 (nand_7_out, B_2, B_2);
  nand nand_8 (nand_8_out, A_2, nand_2_out, C_2);
  nand nand_9 (nand_9_out, A_2, B_2, nand_3_out);
  nand nand_10 (nand_10_out, nand_1_out, C_2);
  nand nand_11 (nand_11_out, B_2, nand_3_out);
  nand nand_12 (nand_12_out, nand_1_out, C_2);
  nand nand_13 (nand_13_out, A_2, nand_3_out);
  nand nand_14 (nand_14_out, nand_1_out, C_2);
  nand nand_15 (nand_15_out, B_2, nand_3_out);
  nand nand_16 (nand_16_out, A_2, nand_2_out);
  nand nand_17 (nand_17_out, nand_4_out, nand_4_out);
  nand nand_18 (nand_18_out, nand_5_out, nand_5_out);
  nand nand_19 (nand_19_out, nand_8_out, nand_8_out);
  nand nand_20 (nand_20_out, nand_9_out, nand_9_out);
  nand nand_21 (nand_21_out, nand_10_out, nand_10_out);
  nand nand_22 (nand_22_out, nand_11_out, nand_11_out);
  nand nand_23 (nand_23_out, nand_12_out, nand_12_out);
  nand nand_24 (nand_24_out, nand_13_out, nand_13_out);
  nand nand_25 (nand_25_out, nand_14_out, nand_14_out);
  nand nand_26 (nand_26_out, nand_15_out, nand_15_out);
  nand nand_27 (nand_27_out, nand_16_out, nand_16_out);
  nand nand_28 (nand_28_out, nand_17_out, nand_17_out);
  nand nand_29 (nand_29_out, nand_18_out, nand_18_out);
  nand nand_30 (nand_30_out, nand_6_out, nand_7_out);
  nand nand_31 (nand_31_out, nand_19_out, nand_19_out);
  nand nand_32 (nand_32_out, nand_20_out, nand_20_out);
  nand nand_33 (nand_33_out, nand_21_out, nand_21_out);
  nand nand_34 (nand_34_out, nand_22_out, nand_22_out);
  nand nand_35 (nand_35_out, nand_23_out, nand_23_out);
  nand nand_36 (nand_36_out, nand_24_out, nand_24_out);
  nand nand_37 (nand_37_out, nand_25_out, nand_25_out);
  nand nand_38 (nand_38_out, nand_26_out, nand_26_out);
  nand nand_39 (nand_39_out, nand_27_out, nand_27_out);
  nand nand_40 (nand_40_out, nand_28_out, nand_29_out);
  nand nand_41 (nand_41_out, nand_31_out, nand_32_out);
  nand nand_42 (nand_42_out, nand_33_out, nand_34_out);
  nand nand_43 (nand_43_out, nand_35_out, nand_36_out);
  nand nand_44 (nand_44_out, nand_37_out, nand_38_out, nand_39_out);
  _7_Segment_Display u_7_segment_display_1 (
    .g(nand_44_out), .f(nand_43_out), .a(nand_40_out), .b(A_2), .e(nand_42_out), .d(nand_41_out),
    .c(nand_30_out));  // open: dp
  nand nand_45 (nand_45_out, A, A);
  nand nand_46 (nand_46_out, B, B);
  nand nand_47 (nand_47_out, C, C);
  nand nand_48 (nand_48_out, A, B, nand_47_out);
  nand nand_49 (nand_49_out, nand_46_out, C);
  nand nand_50 (nand_50_out, A, A);
  nand nand_51 (nand_51_out, B, B);
  nand nand_52 (nand_52_out, A, nand_46_out, C);
  nand nand_53 (nand_53_out, A, B, nand_47_out);
  nand nand_54 (nand_54_out, nand_45_out, C);
  nand nand_55 (nand_55_out, B, nand_47_out);
  nand nand_56 (nand_56_out, nand_45_out, C);
  nand nand_57 (nand_57_out, A, nand_47_out);
  nand nand_58 (nand_58_out, nand_45_out, C);
  nand nand_59 (nand_59_out, B, nand_47_out);
  nand nand_60 (nand_60_out, A, nand_46_out);
  nand nand_61 (nand_61_out, nand_52_out, nand_53_out);
  nand nand_62 (nand_62_out, nand_48_out, nand_49_out);
  nand nand_63 (nand_63_out, nand_50_out, nand_51_out);
  nand nand_64 (nand_64_out, nand_54_out, nand_55_out);
  nand nand_65 (nand_65_out, nand_56_out, nand_57_out);
  nand nand_66 (nand_66_out, nand_58_out, nand_59_out, nand_60_out);
  _7_Segment_Display u_7_segment_display_2 (
    .g(nand_66_out), .f(nand_65_out), .a(nand_62_out), .b(A), .e(nand_64_out), .d(nand_61_out),
    .c(nand_63_out));  // open: dp

  // Notes on the sheet:
  //   b
  //   c
  //   d
  //   e
  //   f
  //   g
  //   a
  //   a
  //   b
  //   c
  //   d
  //   e
  //   f
  //   g
endmodule

module Simplified_SOP_using_NOR_gate (
  input  A,
  input  B,
  input  C
);

  wire nor_1_out, nor_2_out, nor_3_out, nor_4_out, nor_5_out, nor_6_out, nor_7_out, nor_8_out, nor_9_out,
       nor_10_out, nor_11_out, nor_12_out, nor_13_out, nor_14_out, nor_15_out, nor_16_out, nor_17_out,
       nor_18_out, nor_19_out, nor_20_out, nor_21_out, nor_22_out, nor_23_out, nor_24_out, nor_25_out,
       nor_26_out;

  nor nor_1 (nor_1_out, A, A);
  nor nor_2 (nor_2_out, B, B);
  nor nor_3 (nor_3_out, C, C);
  nor nor_4 (nor_4_out, nor_1_out, nor_2_out, C);
  nor nor_5 (nor_5_out, B, nor_3_out);
  nor nor_6 (nor_6_out, nor_1_out, B, nor_3_out);
  nor nor_7 (nor_7_out, nor_1_out, nor_2_out, C);
  nor nor_8 (nor_8_out, A, nor_3_out);
  nor nor_9 (nor_9_out, nor_2_out, C);
  nor nor_10 (nor_10_out, A, nor_3_out);
  nor nor_11 (nor_11_out, nor_1_out, C);
  nor nor_12 (nor_12_out, nor_1_out, C);
  nor nor_13 (nor_13_out, B, nor_3_out);
  nor nor_14 (nor_14_out, A, nor_2_out);
  nor nor_15 (nor_15_out, nor_4_out, nor_5_out);
  nor nor_16 (nor_16_out, A, B);
  nor nor_17 (nor_17_out, nor_6_out, nor_7_out);
  nor nor_18 (nor_18_out, nor_8_out, nor_9_out);
  nor nor_19 (nor_19_out, nor_10_out, nor_11_out);
  nor nor_20 (nor_20_out, nor_12_out, nor_13_out, nor_14_out);
  nor nor_21 (nor_21_out, nor_16_out, nor_16_out);
  nor nor_22 (nor_22_out, nor_15_out, nor_15_out);
  nor nor_23 (nor_23_out, nor_17_out, nor_17_out);
  nor nor_24 (nor_24_out, nor_18_out, nor_18_out);
  nor nor_25 (nor_25_out, nor_19_out, nor_19_out);
  nor nor_26 (nor_26_out, nor_20_out, nor_20_out);
  _7_Segment_Display u_7_segment_display_1 (
    .g(nor_26_out), .f(nor_25_out), .a(nor_22_out), .b(A), .e(nor_24_out), .d(nor_23_out), .c(nor_21_out));  // open: dp

  // Notes on the sheet:
  //   b
  //   c
  //   d
  //   e
  //   f
  //   g
  //   a
endmodule

module Simplified_POS_using_NAND_gate (
  input  A,
  input  B,
  input  C
);

  wire nand_1_out, nand_2_out, nand_3_out, nand_4_out, nand_5_out, nand_6_out, nand_7_out, nand_8_out,
       nand_9_out, nand_10_out, nand_11_out, nand_12_out, nand_13_out, nand_14_out, nand_15_out, nand_16_out,
       nand_17_out, nand_18_out, nand_19_out, nand_20_out, nand_21_out, nand_22_out, not_1_out, not_2_out,
       not_3_out;

  not not_1 (not_1_out, A);
  not not_2 (not_2_out, B);
  not not_3 (not_3_out, C);
  nand nand_1 (nand_1_out, not_1_out, not_3_out);
  nand nand_2 (nand_2_out, not_2_out, not_3_out);
  nand nand_3 (nand_3_out, B, C);
  nand nand_4 (nand_4_out, not_1_out, not_2_out);
  nand nand_5 (nand_5_out, not_2_out, not_3_out);
  nand nand_6 (nand_6_out, B, C);
  nand nand_7 (nand_7_out, not_2_out, not_3_out);
  nand nand_8 (nand_8_out, A, C);
  nand nand_9 (nand_9_out, not_1_out, not_3_out);
  nand nand_10 (nand_10_out, A, C);
  nand nand_11 (nand_11_out, not_1_out, not_2_out, not_3_out);
  nand nand_12 (nand_12_out, A, B, C);
  nand nand_13 (nand_13_out, nand_1_out, nand_2_out, nand_3_out);
  nand nand_14 (nand_14_out, A, nand_5_out, nand_6_out);
  nand nand_15 (nand_15_out, nand_7_out, nand_8_out);
  nand nand_16 (nand_16_out, nand_9_out, nand_10_out);
  nand nand_17 (nand_17_out, nand_11_out, nand_12_out);
  nand nand_18 (nand_18_out, nand_13_out, nand_13_out);
  nand nand_19 (nand_19_out, nand_14_out, nand_14_out);
  nand nand_20 (nand_20_out, nand_15_out, nand_15_out);
  nand nand_21 (nand_21_out, nand_16_out, nand_16_out);
  nand nand_22 (nand_22_out, nand_17_out, nand_17_out);
  _7_Segment_Display u_7_segment_display_1 (
    .g(nand_22_out), .f(nand_21_out), .a(nand_18_out), .b(A), .e(nand_20_out), .d(nand_19_out), .c(nand_4_out));  // open: dp

  // Notes on the sheet:
  //   b
  //   c
  //   a
  //   d
  //   e
  //   f
  //   g
endmodule

module Simplified_POS_using_NOR_gate (
  input  A,
  input  B,
  input  C,
  input  A_2,
  input  B_2,
  input  C_2
);

  wire nor_1_out, nor_2_out, nor_3_out, nor_4_out, nor_5_out, nor_6_out, nor_7_out, nor_8_out, nor_9_out,
       nor_10_out, nor_11_out, nor_12_out, nor_13_out, nor_14_out, nor_15_out, nor_16_out, nor_17_out,
       nor_18_out, nor_19_out, nor_20_out, nor_21_out, nor_22_out, nor_23_out, nor_24_out, nor_25_out,
       nor_26_out, nor_27_out, nor_28_out, nor_29_out, nor_30_out, nor_31_out, nor_32_out, nor_33_out,
       nor_34_out, nor_35_out, nor_36_out, nor_37_out, nor_38_out, nor_39_out, nor_40_out, nor_41_out,
       nor_42_out, nor_43_out, nor_44_out, nor_45_out, nor_46_out, nor_47_out, nor_48_out, nor_49_out,
       nor_50_out, nor_51_out, nor_52_out, nor_53_out, nor_54_out, nor_55_out, nor_56_out, nor_57_out,
       nor_58_out, not_1_out, not_2_out, not_3_out, not_4_out, not_5_out, not_6_out;

  not not_1 (not_1_out, A);
  not not_2 (not_2_out, B);
  not not_3 (not_3_out, C);
  nor nor_1 (nor_1_out, A, C);
  nor nor_2 (nor_2_out, B, C);
  nor nor_3 (nor_3_out, not_2_out, not_3_out);
  nor nor_4 (nor_4_out, A, B);
  nor nor_5 (nor_5_out, B, C);
  nor nor_6 (nor_6_out, not_2_out, not_3_out);
  nor nor_7 (nor_7_out, B, C);
  nor nor_8 (nor_8_out, not_1_out, not_3_out);
  nor nor_9 (nor_9_out, A, C);
  nor nor_10 (nor_10_out, not_1_out, not_3_out);
  nor nor_11 (nor_11_out, A, B, C);
  nor nor_12 (nor_12_out, not_1_out, not_2_out, not_3_out);
  nor nor_13 (nor_13_out, nor_1_out, nor_1_out);
  nor nor_14 (nor_14_out, nor_2_out, nor_2_out);
  nor nor_15 (nor_15_out, nor_3_out, nor_3_out);
  nor nor_16 (nor_16_out, nor_4_out, nor_4_out);
  nor nor_17 (nor_17_out, nor_5_out, nor_5_out);
  nor nor_18 (nor_18_out, nor_6_out, nor_6_out);
  nor nor_19 (nor_19_out, nor_7_out, nor_7_out);
  nor nor_20 (nor_20_out, nor_8_out, nor_8_out);
  nor nor_21 (nor_21_out, nor_9_out, nor_9_out);
  nor nor_22 (nor_22_out, nor_10_out, nor_10_out);
  nor nor_23 (nor_23_out, nor_11_out, nor_11_out);
  nor nor_24 (nor_24_out, nor_12_out, nor_12_out);
  nor nor_25 (nor_25_out, nor_13_out, nor_13_out);
  nor nor_26 (nor_26_out, nor_14_out, nor_14_out);
  nor nor_27 (nor_27_out, nor_15_out, nor_15_out);
  nor nor_28 (nor_28_out, nor_17_out, nor_17_out);
  nor nor_29 (nor_29_out, nor_18_out, nor_18_out);
  nor nor_30 (nor_30_out, nor_19_out, nor_19_out);
  nor nor_31 (nor_31_out, nor_20_out, nor_20_out);
  nor nor_32 (nor_32_out, nor_21_out, nor_21_out);
  nor nor_33 (nor_33_out, nor_22_out, nor_22_out);
  nor nor_34 (nor_34_out, nor_23_out, nor_23_out);
  nor nor_35 (nor_35_out, nor_24_out, nor_24_out);
  nor nor_36 (nor_36_out, nor_25_out, nor_26_out, nor_27_out);
  nor nor_37 (nor_37_out, not_1_out, nor_28_out, nor_29_out);
  nor nor_38 (nor_38_out, nor_30_out, nor_31_out);
  nor nor_39 (nor_39_out, nor_32_out, nor_33_out);
  nor nor_40 (nor_40_out, nor_34_out, nor_35_out);
  _7_Segment_Display u_7_segment_display_1 (
    .g(nor_40_out), .f(nor_39_out), .a(nor_36_out), .b(A), .e(nor_38_out), .d(nor_37_out), .c(nor_16_out));  // open: dp
  not not_4 (not_4_out, A_2);
  not not_5 (not_5_out, B_2);
  not not_6 (not_6_out, C_2);
  nor nor_41 (nor_41_out, A_2, C_2);
  nor nor_42 (nor_42_out, B_2, C_2);
  nor nor_43 (nor_43_out, not_5_out, not_6_out);
  nor nor_44 (nor_44_out, A_2, B_2);
  nor nor_45 (nor_45_out, B_2, C_2);
  nor nor_46 (nor_46_out, not_5_out, not_6_out);
  nor nor_47 (nor_47_out, B_2, C_2);
  nor nor_48 (nor_48_out, not_4_out, not_6_out);
  nor nor_49 (nor_49_out, A_2, C_2);
  nor nor_50 (nor_50_out, not_4_out, not_6_out);
  nor nor_51 (nor_51_out, A_2, B_2, C_2);
  nor nor_52 (nor_52_out, not_4_out, not_5_out, not_6_out);
  nor nor_53 (nor_53_out, nor_41_out, nor_42_out, nor_43_out);
  nor nor_54 (nor_54_out, nor_44_out, nor_44_out);
  nor nor_55 (nor_55_out, not_4_out, nor_45_out, nor_46_out);
  nor nor_56 (nor_56_out, nor_47_out, nor_48_out);
  nor nor_57 (nor_57_out, nor_49_out, nor_50_out);
  nor nor_58 (nor_58_out, nor_51_out, nor_52_out);
  _7_Segment_Display u_7_segment_display_2 (
    .g(nor_58_out), .f(nor_57_out), .a(nor_53_out), .b(A_2), .e(nor_56_out), .d(nor_55_out), .c(nor_54_out));  // open: dp

  // Notes on the sheet:
  //   b
  //   c
  //   d
  //   e
  //   f
  //   g
  //   a
  //   d
  //   e
  //   f
  //   g
  //   b
  //   c
  //   a
endmodule

module Circuit_Implementation_with_Decoder (
  input  [2:0] A_B_C
);

  wire decoder_1_out0, decoder_1_out1, decoder_1_out2, decoder_1_out3, decoder_1_out4, decoder_1_out5,
       decoder_1_out6, decoder_1_out7, or_1_out, or_2_out, or_3_out, or_4_out, or_5_out, or_6_out, or_7_out,
       or_8_out, or_9_out, or_10_out, or_11_out, or_12_out, or_13_out, or_14_out, or_15_out, or_16_out;

  Decoder #(.select(3), .enable("false")) decoder_1 (
    .out0(decoder_1_out0), .out1(decoder_1_out1), .out2(decoder_1_out2), .out3(decoder_1_out3),
    .out4(decoder_1_out4), .out5(decoder_1_out5), .out6(decoder_1_out6), .out7(decoder_1_out7), .sel(A_B_C));
  or or_1 (or_1_out, decoder_1_out6, decoder_1_out5, decoder_1_out1);
  or or_2 (or_2_out, decoder_1_out7, decoder_1_out6, decoder_1_out5);
  or or_3 (or_3_out, decoder_1_out7, decoder_1_out6, decoder_1_out5);
  or or_4 (or_4_out, decoder_1_out2, decoder_1_out3, decoder_1_out6);
  or or_5 (or_5_out, decoder_1_out5, decoder_1_out6);
  or or_6 (or_6_out, decoder_1_out3, decoder_1_out1, decoder_1_out6);
  or or_7 (or_7_out, decoder_1_out3, decoder_1_out1, decoder_1_out6);
  or or_8 (or_8_out, or_2_out, decoder_1_out4);
  or or_9 (or_9_out, or_3_out, decoder_1_out4);
  or or_10 (or_10_out, or_4_out, decoder_1_out7);
  or or_11 (or_11_out, or_6_out, decoder_1_out2);
  or or_12 (or_12_out, or_7_out, decoder_1_out4);
  or or_13 (or_13_out, decoder_1_out3, decoder_1_out1, decoder_1_out6);
  or or_14 (or_14_out, or_13_out, decoder_1_out5, decoder_1_out2);
  or or_15 (or_15_out, or_9_out, or_10_out);
  or or_16 (or_16_out, or_14_out, decoder_1_out4);
  _7_Segment_Display u_7_segment_display_1 (
    .g(or_16_out), .f(or_12_out), .a(or_1_out), .b(or_8_out), .e(or_11_out), .d(or_5_out), .c(or_15_out));  // open: dp

  // Notes on the sheet:
  //   A'B'C'
  //   A'BC'
  //   A'BC
  //   A'B'C
  //   AB'C'
  //   AB'C
  //   ABC'
  //   ABC
  //   a
  //   b
  //   d
  //   e
  //   f
  //   g
  //   c
endmodule

module Circuit_Implementation_with_Multiplexer (
  input  A,
  input  B,
  input  C,
  input  A_2,
  input  B_2,
  input  C_2
);

  wire multiplexer_1_out, multiplexer_2_out, multiplexer_3_out, multiplexer_4_out, multiplexer_5_out,
       multiplexer_6_out, multiplexer_7_out, multiplexer_8_out, multiplexer_9_out, multiplexer_10_out,
       multiplexer_11_out, multiplexer_12_out, multiplexer_13_out, multiplexer_14_out, not_2_out;

  Multiplexer #(.select(3), .enable("false")) multiplexer_1 (
    .in0(1'b0), .in1(1'b1), .in2(1'b0), .in3(1'b0), .in4(1'b0), .in5(1'b1), .in6(1'b1), .in7(1'b0),
    .out(multiplexer_1_out), .sel({A, B, C}));
  Multiplexer #(.select(3), .enable("false")) multiplexer_2 (
    .in0(1'b0), .in1(1'b0), .in2(1'b0), .in3(1'b0), .in4(1'b1), .in5(1'b1), .in6(1'b1), .in7(1'b1),
    .out(multiplexer_2_out), .sel({A, B, C}));
  Multiplexer #(.select(3), .enable("false")) multiplexer_3 (
    .in0(1'b0), .in1(1'b0), .in2(1'b1), .in3(1'b1), .in4(1'b1), .in5(1'b1), .in6(1'b1), .in7(1'b1),
    .out(multiplexer_3_out), .sel({A, B, C}));
  Multiplexer #(.select(3), .enable("false")) multiplexer_4 (
    .in0(1'b0), .in1(1'b0), .in2(1'b0), .in3(1'b0), .in4(1'b0), .in5(1'b1), .in6(1'b1), .in7(1'b0),
    .out(multiplexer_4_out), .sel({A, B, C}));
  Multiplexer #(.select(3), .enable("false")) multiplexer_5 (
    .in0(1'b0), .in1(1'b1), .in2(1'b1), .in3(1'b1), .in4(1'b0), .in5(1'b0), .in6(1'b1), .in7(1'b0),
    .out(multiplexer_5_out), .sel({A, B, C}));
  Multiplexer #(.select(3), .enable("false")) multiplexer_6 (
    .in0(1'b0), .in1(1'b1), .in2(1'b0), .in3(1'b1), .in4(1'b1), .in5(1'b0), .in6(1'b1), .in7(1'b0),
    .out(multiplexer_6_out), .sel({A, B, C}));
  Multiplexer #(.select(3), .enable("false")) multiplexer_7 (
    .in0(1'b0), .in1(1'b1), .in2(1'b1), .in3(1'b1), .in4(1'b1), .in5(1'b1), .in6(1'b1), .in7(1'b0),
    .out(multiplexer_7_out), .sel({A, B, C}));
  _7_Segment_Display u_7_segment_display_1 (
    .g(multiplexer_7_out), .f(multiplexer_6_out), .a(multiplexer_1_out), .b(multiplexer_2_out),
    .e(multiplexer_5_out), .d(multiplexer_4_out), .c(multiplexer_3_out));  // open: dp
  // NOT_Gate not_1 has open pins: in=B_2, out=open
  not not_2 (not_2_out, C_2);
  Multiplexer #(.select(2), .enable("false")) multiplexer_8 (
    .in0(C_2), .in1(1'b0), .in2(C_2), .in3(not_2_out), .out(multiplexer_8_out), .sel({A_2, B_2}));
  Multiplexer #(.select(2), .enable("false")) multiplexer_9 (
    .in0(A_2), .in1(A_2), .in2(A_2), .in3(A_2), .out(multiplexer_9_out), .sel({B_2, C_2}));
  Multiplexer #(.select(3), .enable("false")) multiplexer_10 (
    .in0(1'b0), .in1(1'b0), .in2(1'b1), .in3(1'b1), .in4(1'b1), .in5(1'b1), .in6(1'b1), .in7(1'b1),
    .out(multiplexer_10_out), .sel({A_2, B_2, C_2}));
  Multiplexer #(.select(2), .enable("false")) multiplexer_11 (
    .in0(1'b0), .in1(1'b0), .in2(C_2), .in3(not_2_out), .out(multiplexer_11_out), .sel({A_2, B_2}));
  Multiplexer #(.select(2), .enable("false")) multiplexer_12 (
    .in0(C_2), .in1(1'b1), .in2(1'b0), .in3(not_2_out), .out(multiplexer_12_out), .sel({A_2, B_2}));
  Multiplexer #(.select(2), .enable("false")) multiplexer_13 (
    .in0(C_2), .in1(C_2), .in2(not_2_out), .in3(not_2_out), .out(multiplexer_13_out), .sel({A_2, B_2}));
  Multiplexer #(.select(2), .enable("false")) multiplexer_14 (
    .in0(C_2), .in1(1'b1), .in2(1'b1), .in3(not_2_out), .out(multiplexer_14_out), .sel({A_2, B_2}));
  _7_Segment_Display u_7_segment_display_2 (
    .g(multiplexer_14_out), .f(multiplexer_13_out), .a(multiplexer_8_out), .b(multiplexer_9_out),
    .e(multiplexer_12_out), .d(multiplexer_11_out), .c(multiplexer_10_out));  // open: dp

  // Notes on the sheet:
  //   a
  //   b
  //   c
  //   d
  //   e
  //   f
  //   g
endmodule
