// Logisim project 2021183642_Fahim Muntashir.circ as structural Verilog: 1 circuit, main circuit main
module main (
  input  A,
  input  B,
  input  C,
  output out_4,
  output out_5
);

  wire and_1_out, and_2_out, and_3_out, decoder_1_out0, decoder_1_out1, decoder_1_out2, decoder_1_out3,
       decoder_2_out0, decoder_2_out1, decoder_2_out2, decoder_2_out3, not_1_out, not_2_out, not_3_out,
       or_2_out;

  not not_1 (not_1_out, A);
  not not_2 (not_2_out, B);
  not not_3 (not_3_out, C);
  and and_1 (and_1_out, B, not_3_out);
  and and_2 (and_2_out, A, B);
  and and_3 (and_3_out, not_1_out, not_2_out, C);
  Decoder #(.select(2)) decoder_1 (
    .out0(decoder_1_out0), .out1(decoder_1_out1), .out2(decoder_1_out2), .out3(decoder_1_out3), .sel({B, C}),
    .en(not_1_out));
  Decoder #(.select(2)) decoder_2 (
    .out0(decoder_2_out0), .out1(decoder_2_out1), .out2(decoder_2_out2), .out3(decoder_2_out3), .sel({B, C}),
    .en(A));
  or or_1 (out_4, and_1_out, and_2_out, and_3_out);
  or or_2 (or_2_out, decoder_1_out1, decoder_1_out2, decoder_2_out2);
  or or_3 (out_5, or_2_out, decoder_2_out3);

  // Notes on the sheet:
  //   y= BC'+AB+A'B'C
  //   Basic gates
endmodule
